// Digital circuit CPU.dig as structural Verilog
module CPU (
  input  Slow,
  input  Fast
);

  wire and_1_out, and_2_out, and_3_out, and_4_out, AR_In, AR_Out, AR_Sel, button_1_out, button_2_out,
       button_3_out, button_4_out, Clk, Clk_t, counter_1_ovf, counterpreset_1_ovf, decoder_1_out_0,
       decoder_1_out_1, decoder_1_out_2, decoder_1_out_3, demultiplexer_1_out_0, demultiplexer_1_out_1,
       demultiplexer_1_out_2, demultiplexer_1_out_3, demultiplexer_1_out_4, demultiplexer_1_out_5,
       demultiplexer_1_out_6, demultiplexer_1_out_8, dipswitch_1_out, dipswitch_26_out, IR_In, IR_Out,
       Jump_out, MA_In, MD_In, MD_Out, MP_In, not_1_out, not_4_out, or_1_out, or_2_out, or_3_out, or_4_out,
       or_5_out, or_6_out, or_7_out, or_8_out, or_9_out, or_10_out, or_11_out, or_12_out, PC_In, PC_Inc,
       PC_Out, Reset_to_0_out, rs_ff_as_1_q, rs_ff_as_2_q, rs_ff_as_3_q, rs_ff_as_4_q, SC_Res, ShdwCpAct,
       Step_out;
  wire [2:0] Stp_Cnt_out;
  wire [3:0] register_1_q;
  wire [4:0] Mem_Page_q;
  wire [5:0] counterpreset_1_out, Mem_Addr_q, multiplexer_2_out;
  wire [7:0] alu_1_outa, alu_1_outb, alu_1_q, Boot_ROM_d, Bus, dipswitch_18_out, GP_A_q, GP_B_q, GP_C_q,
       GP_D_q, GP_E_q, Inst_Reg_q, multiplexer_4_out;
  wire [10:0] counter_1_out, multiplexer_3_out;
  wire [15:0] dipswitch_2_out, Microcode_d, multiplexer_1_out;

  DipSwitch dipswitch_1 (.out(dipswitch_1_out));
  DipSwitch dipswitch_2 (.out(dipswitch_2_out[15]));
  DipSwitch dipswitch_3 (.out(dipswitch_2_out[14]));
  DipSwitch dipswitch_4 (.out(dipswitch_2_out[13]));
  DipSwitch dipswitch_5 (.out(dipswitch_2_out[12]));
  DipSwitch dipswitch_6 (.out(dipswitch_2_out[11]));
  DipSwitch dipswitch_7 (.out(dipswitch_2_out[10]));
  DipSwitch dipswitch_8 (.out(dipswitch_2_out[9]));
  DipSwitch dipswitch_9 (.out(dipswitch_2_out[8]));
  DipSwitch dipswitch_10 (.out(dipswitch_2_out[7]));
  DipSwitch dipswitch_11 (.out(dipswitch_2_out[6]));
  DipSwitch dipswitch_12 (.out(dipswitch_2_out[5]));
  DipSwitch dipswitch_13 (.out(dipswitch_2_out[4]));
  DipSwitch dipswitch_14 (.out(dipswitch_2_out[3]));
  DipSwitch dipswitch_15 (.out(dipswitch_2_out[2]));
  DipSwitch dipswitch_16 (.out(dipswitch_2_out[1]));
  DipSwitch dipswitch_17 (.out(dipswitch_2_out[0]));
  Register #(.Bits(8)) Inst_Reg (.D(Bus), .C(Clk), .en(IR_In), .Q(Inst_Reg_q));
  Button Jump (.out(Jump_out));
  Multiplexer #(.Bits(16)) multiplexer_1 (
    .sel(dipswitch_1_out), .in_0(Microcode_d), .in_1(dipswitch_2_out), .out(multiplexer_1_out));
  assign Bus = IR_Out ? Inst_Reg_q : 8'bz;  // Driver driver_1
  CounterPreset #(.Bits(6)) counterpreset_1 (
    .en(PC_Inc), .C(Clk), .dir(1'b0), .in(Bus[5:0]), .ld(Jump_out), .clr(Reset_to_0_out),
    .out(counterpreset_1_out), .ovf(counterpreset_1_ovf));
  Button Reset_to_0 (.out(Reset_to_0_out));
  LED Control_Overrides (.in(dipswitch_1_out));
  ROM #(.bigEndian("true"), .AddrBits(5), .Bits(16)) Microcode (
    .A({Inst_Reg_q[7:6], Stp_Cnt_out}), .sel(1'b1), .D(Microcode_d));
  Multiplexer #(.Bits(16)) multiplexer_2 (
    .sel(ShdwCpAct), .in_0(multiplexer_1_out), .in_1({16{1'b0}}),
    .out({MP_In, MA_In, MD_In, MD_Out, AR_Sel, AR_In, AR_Out, PC_Inc, PC_In, PC_Out, multiplexer_2_out[5], SC_Res, IR_In, IR_Out, multiplexer_2_out[1:0]}));
  Counter #(.Bits(3)) Stp_Cnt (.en(not_1_out), .C(Clk), .clr(SC_Res), .out(Stp_Cnt_out));  // open: ovf
  LED Overflow (.in(counterpreset_1_ovf));
  assign Bus = PC_Out ? {2'b00, counterpreset_1_out} : 8'bz;  // Driver driver_2
  not not_1 (not_1_out, ShdwCpAct);
  DipSwitch dipswitch_18 (.out(dipswitch_18_out[7]));
  DipSwitch dipswitch_19 (.out(dipswitch_18_out[6]));
  DipSwitch dipswitch_20 (.out(dipswitch_18_out[5]));
  DipSwitch dipswitch_21 (.out(dipswitch_18_out[4]));
  DipSwitch dipswitch_22 (.out(dipswitch_18_out[3]));
  DipSwitch dipswitch_23 (.out(dipswitch_18_out[2]));
  DipSwitch dipswitch_24 (.out(dipswitch_18_out[1]));
  DipSwitch dipswitch_25 (.out(dipswitch_18_out[0]));
  Counter #(.Bits(11)) counter_1 (.en(ShdwCpAct), .C(Clk), .clr(1'b0), .out(counter_1_out), .ovf(counter_1_ovf));
  PullDown pulldown_1 (.out(counter_1_ovf));
  DipSwitch dipswitch_26 (.out(dipswitch_26_out));
  assign Bus = dipswitch_26_out ? dipswitch_18_out : 8'bz;  // Driver driver_3
  Register #(.Bits(5)) Mem_Page (.D(Bus[4:0]), .C(Clk), .en(MP_In), .Q(Mem_Page_q));
  Register #(.Bits(6)) Mem_Addr (.D(Bus[5:0]), .C(Clk), .en(MA_In), .Q(Mem_Addr_q));
  or or_1 (or_1_out, counter_1_ovf, or_1_out);
  PullDown pulldown_2 (.out(or_1_out));
  LED led_1 (.in(Bus[7]));
  LED led_2 (.in(Bus[6]));
  ROM #(.AddrBits(11), .Bits(8)) Boot_ROM (.A(counter_1_out), .sel(ShdwCpAct), .D(Boot_ROM_d));
  LED led_3 (.in(Bus[5]));
  LED led_4 (.in(Bus[4]));
  Seven_Seg_Hex seven_seg_hex_1 (.d({3'b000, Mem_Page_q[4]}), .dp(1'b0));
  Multiplexer #(.Bits(11)) multiplexer_3 (
    .sel(ShdwCpAct), .in_0({{5{1'b0}}, Mem_Addr_q}), .in_1(counter_1_out), .out(multiplexer_3_out));
  not not_2 (ShdwCpAct, or_1_out);
  LED led_5 (.in(Bus[3]));
  LED led_6 (.in(Bus[2]));
  PullDown #(.Bits(8)) pulldown_3 (.out(Bus));
  Seven_Seg_Hex seven_seg_hex_2 (.d(Mem_Page_q[3:0]), .dp(1'b0));
  // Probe Address on multiplexer_3_out
  assign Bus = ShdwCpAct ? Boot_ROM_d : 8'bz;  // Driver driver_4
  LED led_7 (.in(Bus[1]));
  LED led_8 (.in(Bus[0]));
  Seven_Seg_Hex seven_seg_hex_3 (.d({2'b00, Mem_Addr_q[5:4]}), .dp(1'b0));
  or or_2 (or_2_out, MD_In, ShdwCpAct);
  Seven_Seg_Hex seven_seg_hex_4 (.d(Bus[7:4]), .dp(1'b0));
  Seven_Seg_Hex seven_seg_hex_5 (.d(Mem_Addr_q[3:0]), .dp(1'b0));
  RAMSinglePort #(.AddrBits(11), .Bits(8)) ramsingleport_1 (
    .A(multiplexer_3_out), .str(or_2_out), .C(Clk), .ld(MD_Out), .D(Bus));
  Seven_Seg_Hex seven_seg_hex_6 (.d(Bus[3:0]), .dp(1'b0));
  // Probe Data on Bus
  or or_3 (or_3_out, button_1_out, and_2_out);
  Button button_1 (.out(button_1_out));
  Button button_2 (.out(button_2_out));
  Button button_3 (.out(button_3_out));
  Button button_4 (.out(button_4_out));
  and and_1 (and_1_out, decoder_1_out_1, 1'b0);
  and and_2 (and_2_out, decoder_1_out_0, 1'b0);
  Decoder #(.Selector_Bits(2)) decoder_1 (
    .sel(2'b00), .out_0(decoder_1_out_0), .out_1(decoder_1_out_1), .out_2(decoder_1_out_2),
    .out_3(decoder_1_out_3));
  or or_4 (or_4_out, button_3_out, or_5_out);
  or or_5 (or_5_out, and_3_out, not_4_out);
  and and_3 (and_3_out, decoder_1_out_2, 1'b0);
  or or_6 (or_6_out, button_2_out, and_1_out);
  or or_7 (or_7_out, button_4_out, and_4_out);
  and and_4 (and_4_out, decoder_1_out_3, 1'b0);
  Register #(.Bits(4)) register_1 (.D(Bus[3:0]), .C(Clk), .en(AR_Sel), .Q(register_1_q));
  Demultiplexer #(.Selector_Bits(4)) demultiplexer_1 (
    .sel(register_1_q), .in(AR_In), .out_0(demultiplexer_1_out_0), .out_1(demultiplexer_1_out_1),
    .out_2(demultiplexer_1_out_2), .out_3(demultiplexer_1_out_3), .out_4(demultiplexer_1_out_4),
    .out_5(demultiplexer_1_out_5), .out_6(demultiplexer_1_out_6), .out_8(demultiplexer_1_out_8));  // open: out_7, out_9, out_10, out_11, out_12, out_13, out_14, out_15
  LED led_9 (.in(rs_ff_as_1_q));
  LED led_10 (.in(rs_ff_as_3_q));
  LED led_11 (.in(rs_ff_as_2_q));
  LED led_12 (.in(rs_ff_as_4_q));
  or or_8 (or_8_out, or_6_out, or_4_out, or_7_out);
  or or_9 (or_9_out, or_3_out, or_4_out, or_7_out);
  or or_10 (or_10_out, or_3_out, or_6_out, or_7_out);
  or or_11 (or_11_out, or_3_out, or_6_out, or_4_out);
  RS_FF_AS rs_ff_as_1 (.S(or_3_out), .R(or_8_out), .Q(rs_ff_as_1_q));  // open: nQ
  RS_FF_AS rs_ff_as_2 (.S(or_4_out), .R(or_10_out), .Q(rs_ff_as_2_q));  // open: nQ
  Button Step (.out(Step_out));
  assign Clk = rs_ff_as_1_q ? 1'b0 : 1'bz;  // Driver driver_5
  assign Clk = rs_ff_as_2_q ? Slow : 1'bz;  // Driver driver_6
  RS_FF_AS rs_ff_as_3 (.S(or_6_out), .R(or_9_out), .Q(rs_ff_as_3_q));  // open: nQ
  RS_FF_AS rs_ff_as_4 (.S(or_7_out), .R(or_11_out), .Q(rs_ff_as_4_q));  // open: nQ
  Register #(.Bits(8)) GP_A (.D(Bus), .C(Clk), .en(demultiplexer_1_out_0), .Q(GP_A_q));
  Register #(.Bits(8)) GP_B (.D(Bus), .C(Clk), .en(demultiplexer_1_out_1), .Q(GP_B_q));
  Register #(.Bits(8)) GP_C (.D(Bus), .C(Clk), .en(demultiplexer_1_out_2), .Q(GP_C_q));
  Register #(.Bits(8)) GP_D (.D(Bus), .C(Clk), .en(demultiplexer_1_out_3), .Q(GP_D_q));
  Register #(.Bits(8)) GP_E (.D(Bus), .C(Clk), .en(demultiplexer_1_out_4), .Q(GP_E_q));
  ALU alu_1 (
    .DataIn(Bus), .Clk(Clk), .InA(demultiplexer_1_out_5), .InB(demultiplexer_1_out_6), .Mode(1'b0),
    .OutA(alu_1_outa), .OutB(alu_1_outb), .Q(alu_1_q));
  assign Clk = rs_ff_as_3_q ? Step_out : 1'bz;  // Driver driver_7
  assign Clk = rs_ff_as_4_q ? Fast : 1'bz;  // Driver driver_8
  PullDown pulldown_4 (.out(Clk));
  not not_3 (Clk_t, Clk);
  or or_12 (or_12_out, or_12_out, Clk);
  not not_4 (not_4_out, or_12_out);
  LED led_13 (.in(GP_A_q[7]));
  LED led_14 (.in(GP_A_q[6]));
  LED led_15 (.in(GP_B_q[7]));
  LED led_16 (.in(GP_B_q[6]));
  LED led_17 (.in(GP_C_q[7]));
  LED led_18 (.in(GP_C_q[6]));
  LED led_19 (.in(GP_D_q[7]));
  LED led_20 (.in(GP_D_q[6]));
  LED led_21 (.in(GP_E_q[7]));
  LED led_22 (.in(GP_E_q[6]));
  PullDown pulldown_5 (.out(or_12_out));
  LED led_23 (.in(GP_A_q[5]));
  LED led_24 (.in(GP_A_q[4]));
  LED led_25 (.in(GP_B_q[5]));
  LED led_26 (.in(GP_B_q[4]));
  LED led_27 (.in(GP_C_q[5]));
  LED led_28 (.in(GP_C_q[4]));
  LED led_29 (.in(GP_D_q[5]));
  LED led_30 (.in(GP_D_q[4]));
  LED led_31 (.in(GP_E_q[5]));
  LED led_32 (.in(GP_E_q[4]));
  LED led_33 (.in(alu_1_outa[7]));
  LED led_34 (.in(alu_1_outa[6]));
  LED led_35 (.in(alu_1_outb[7]));
  LED led_36 (.in(alu_1_outb[6]));
  LED led_37 (.in(alu_1_q[7]));
  LED led_38 (.in(alu_1_q[6]));
  LED led_39 (.in(GP_A_q[3]));
  LED led_40 (.in(GP_A_q[2]));
  LED led_41 (.in(GP_B_q[3]));
  LED led_42 (.in(GP_B_q[2]));
  LED led_43 (.in(GP_C_q[3]));
  LED led_44 (.in(GP_C_q[2]));
  LED led_45 (.in(GP_D_q[3]));
  LED led_46 (.in(GP_D_q[2]));
  LED led_47 (.in(GP_E_q[3]));
  LED led_48 (.in(GP_E_q[2]));
  LED led_49 (.in(alu_1_outa[5]));
  LED led_50 (.in(alu_1_outa[4]));
  LED led_51 (.in(alu_1_outb[5]));
  LED led_52 (.in(alu_1_outb[4]));
  LED led_53 (.in(alu_1_q[5]));
  LED led_54 (.in(alu_1_q[4]));
  LED led_55 (.in(GP_A_q[1]));
  LED led_56 (.in(GP_A_q[0]));
  LED led_57 (.in(GP_B_q[1]));
  LED led_58 (.in(GP_B_q[0]));
  LED led_59 (.in(GP_C_q[1]));
  LED led_60 (.in(GP_C_q[0]));
  LED led_61 (.in(GP_D_q[1]));
  LED led_62 (.in(GP_D_q[0]));
  LED led_63 (.in(GP_E_q[1]));
  LED led_64 (.in(GP_E_q[0]));
  LED led_65 (.in(alu_1_outa[3]));
  LED led_66 (.in(alu_1_outa[2]));
  LED led_67 (.in(alu_1_outb[3]));
  LED led_68 (.in(alu_1_outb[2]));
  LED led_69 (.in(alu_1_q[3]));
  LED led_70 (.in(alu_1_q[2]));
  LED led_71 (.in(alu_1_outa[1]));
  LED led_72 (.in(alu_1_outa[0]));
  LED led_73 (.in(alu_1_outb[1]));
  LED led_74 (.in(alu_1_outb[0]));
  LED led_75 (.in(alu_1_q[1]));
  LED led_76 (.in(alu_1_q[0]));
  Multiplexer #(.Selector_Bits(4), .Bits(8)) multiplexer_4 (
    .sel(register_1_q), .in_0(GP_A_q), .in_1(GP_B_q), .in_2(GP_C_q), .in_3(GP_D_q), .in_4(GP_E_q),
    .in_5(alu_1_outa), .in_6(alu_1_outb), .in_7(alu_1_q), .in_8({8{1'b0}}), .in_9({8{1'b0}}),
    .in_10({8{1'b0}}), .in_11({8{1'b0}}), .in_12({8{1'b0}}), .in_13({8{1'b0}}), .in_14({8{1'b0}}),
    .in_15({8{1'b0}}), .out(multiplexer_4_out));
  assign Bus = AR_Out ? multiplexer_4_out : 8'bz;  // Driver driver_9

  // Notes on the sheet:
  //   Slow: Hz: 5
  //   Fast: Hz: 200
  //   Control
  //   Program Counter
  //   Microcode loads Microcode.bin
  //   Bus
  //   Memory
  //   Boot_ROM loads Boot.bin
  //   Mem Page
  //   Mem Addr
  //   Clock
  //   Software Select
  //   Mode latching
  //   For the next register
  //   GP Registers
  //   ALU
  //   Poweron Select
endmodule
